# Fritzing sketch fullschem (saved by Fritzing 0.8.7b)

parts:
  Part1 = Arduino Uno (Rev3)
  U1 = TMP36 [package=to-92-kit]
  U2 = TMP36 [package=to-92-kit]
  PIR1 = PIR sensor
  LED1 = LED - 5mm [color="Red (633nm)" package="5 mm [THT]"]
  R1 = Resistor [tolerance=±5% resistance=220 package=THT]
  R2 = Resistor [tolerance=±5% resistance=10k package=THT]

nets:
  N1: Part1.A0, U1.VOUT
  N2: Part1.A1, U2.VOUT
  N3: Part1.D13/SCK, R1.Pin_0
  GND: Part1.GND, U1.GND, LED1.cathode
  5V: Part1.5V, U1.VCC
  N4: PIR1.GND, R2.Pin_1
